// Logisim project 2_Bit_ALU.circ as structural Verilog: 3 circuits, main circuit main
module main (
  input  carry_in,
  input  [1:0] A,
  input  Binvert,
  input  [1:0] B,
  input  [1:0] Operation,
  output [1:0] result,
  output Zero,
  output overflow,
  output carry_out
);

  _2_Bit_ALU u_2_bit_alu_1 (
    .A(A), .Binvert(Binvert), .B(B), .Operation(Operation), .Result(result), .Zero(Zero),
    .OverFlow(overflow), .CarryOut(carry_out), .Carry_in(carry_in));
endmodule

module _1_Bit_ALU (
  input  B,
  input  A,
  input  Carry_in,
  input  [1:0] Operation,
  input  Binvert,
  output out_6,
  output Carry_out
);

  wire adder_1_out, and_1_out, multiplexer_1_out, not_1_out, or_1_out;

  not not_1 (not_1_out, B);
  Multiplexer multiplexer_1 (.in0(not_1_out), .in1(B), .out(multiplexer_1_out), .sel(Binvert));  // open: en
  and and_1 (and_1_out, A, multiplexer_1_out);
  or or_1 (or_1_out, A, multiplexer_1_out);
  Adder #(.width(1)) adder_1 (.a(A), .b(multiplexer_1_out), .out(adder_1_out), .cin(Carry_in), .cout(Carry_out));
  Multiplexer #(.select(2)) multiplexer_2 (
    .in0(and_1_out), .in1(or_1_out), .in2(adder_1_out), .out(out_6), .sel(Operation));  // open: in3, en
endmodule

module _2_Bit_ALU (
  input  Carry_in,
  input  [1:0] A,
  input  Binvert,
  input  [1:0] B,
  input  [1:0] Operation,
  output [1:0] Result,
  output Zero,
  output OverFlow,
  output CarryOut
);

  wire n1_bit_alu_1_carry_out;

  _1_Bit_ALU u_1_bit_alu_1 (
    .out_6(Result[0]), .B(B[0]), .A(A[0]), .Carry_in(Carry_in), .Binvert(Binvert),
    .Carry_out(n1_bit_alu_1_carry_out), .Operation(Operation));
  _1_Bit_ALU u_1_bit_alu_2 (
    .out_6(Result[1]), .B(B[1]), .A(A[1]), .Carry_in(n1_bit_alu_1_carry_out), .Binvert(Binvert),
    .Carry_out(CarryOut), .Operation(Operation));
  nor nor_1 (Zero, Result[0], Result[1]);
  xor xor_1 (OverFlow, n1_bit_alu_1_carry_out, CarryOut);
endmodule
